# Fritzing sketch midterm_fritz (saved by Fritzing 0.9.4)
breadboards: 1

parts:
  Teensy_3_1 = Teensy 3.1  # not connected
  RG_encoder1 = SprkFn RG Encoder [package="DIP (Dual Inline) [THT]"]
  WIZ820io2 = WIZ820io [part_number=WIZ820io]
  S1 = Pushbutton [package="[THT]"]
  OLED_I2C2 = OLED 128x64 I2C Monochrome Display
  M2 = BMP280
  LED2 = LED - 3mm [color="Red (633nm)" package="3 mm [THT]"]
  LED4 = LED - 3mm [color="Red (633nm)" package="3 mm [THT]"]
  LED5 = LED - 3mm [color="Red (633nm)" package="3 mm [THT]"]
  LED6 = LED - 3mm [color="Red (633nm)" package="3 mm [THT]"]
  R1 = Resistor [tolerance=±5% resistance=220 package=THT]
  R2 = Resistor [tolerance=±5% resistance=220 package=THT]
  R3 = Resistor [tolerance=±5% resistance=220 package=THT]
  R4 = Resistor [tolerance=±5% resistance=220 package=THT]
  R5 = Resistor [tolerance=±5% resistance=220 package=THT]

nets:
  GND: RG_encoder1.GND, WIZ820io2.GND, OLED_I2C2.GND, M2.GND, R1.Pin_0, R2.Pin_0, R3.Pin_0, R4.Pin_0, R5.Pin_0
  VIN: WIZ820io2.VIN, OLED_I2C2.VDD, M2.VIN
  N1: S1.Pin_1, S1.Pin_2
  N2: S1.Pin_3, S1.Pin_4, R5.Pin_1
  N3: OLED_I2C2.SDA, M2.SDA
  N4: OLED_I2C2.SCK, M2.SCL
  N5: LED2.anode, R1.Pin_1
  N6: LED4.anode, R2.Pin_1
  N7: LED5.anode, R3.Pin_1
  N8: LED6.anode, R4.Pin_1

custom parts:
  SprkFn RG Encoder: SparkFun RG Rotary Encoder
  Pushbutton: A generic pushbutton.
  BMP280: Temperature Humidity Barometric presure Sensor, I2C
